# Fritzing sketch robot (saved by Fritzing 0.9.6b)
circuit board: 4cm x 16cm
breadboards: 1

parts:
  HMC5883L = Boladge HMC5883L Compass Module
  Buzzer = Piezo Speaker
  HC-SR04 = mystery part, 4 pins
  Power_5V = Terminal 2pin
  L_motor = Terminal 2pin
  R_motor = Terminal 2pin
  Rotary = Terminal 2pin
  Arduino_Nano_Every = Arduino Nano Every
  C3 = Ceramic Capacitor [capacitance=100nF voltage=35V package="100 mil [THT, multilayer]"]
  C4 = Ceramic Capacitor [capacitance=100nF voltage=35V package="100 mil [THT, multilayer]"]
  C1 = Ceramic Capacitor [capacitance=100nF voltage=35V package="100 mil [THT, multilayer]"]
  C2 = Ceramic Capacitor [capacitance=100nF voltage=35V package="100 mil [THT, multilayer]"]
  Motor_Driver = Adafruit TB6612 DC and Stepper Motor Driver [part_number=TB6612]
  PS2_Receiver = mystery part, 6 pins
  R1 = Resistor [tolerance=±5% power=0.25 resistance=5.6k package=THT]
  R2 = Resistor [tolerance=±5% power=0.25 resistance=5.6k package=THT]
  R3 = Resistor [tolerance=±5% power=0.25 resistance=5.6k package=THT]

nets:
  VCC: HMC5883L.VCC, HC-SR04.pin1, Power_5V.pin_2, Arduino_Nano_Every.+5V, Motor_Driver.VCC
  GND: HMC5883L.GND, Buzzer.pin1, HC-SR04.pin4, Power_5V.pin_1, Arduino_Nano_Every.GND, C3.0, C4.0, Motor_Driver.GND, PS2_Receiver.pin3
  N1: HMC5883L.SCL, Arduino_Nano_Every.A5
  N2: HMC5883L.SDA, Arduino_Nano_Every.A4
  N3: Buzzer.pin2, Arduino_Nano_Every.A3
  N4: HC-SR04.pin2, Arduino_Nano_Every.D6~
  N5: HC-SR04.pin3, Arduino_Nano_Every.D5~
  N6: L_motor.pin_1, C1.0, Motor_Driver.MOTORB2
  N7: L_motor.pin_2, C1.1, Motor_Driver.MOTORB1
  N8: R_motor.pin_1, C2.1, Motor_Driver.MOTORA1
  N9: R_motor.pin_2, C2.0, Motor_Driver.MOTORA2
  N10: Rotary.pin_1, Arduino_Nano_Every.A7, C3.1
  N11: Rotary.pin_2, Arduino_Nano_Every.A6, C4.1
  N12: Arduino_Nano_Every.D2, Motor_Driver.AIN2
  N13: Arduino_Nano_Every.D4, Motor_Driver.AIN1
  N14: Arduino_Nano_Every.D7, Motor_Driver.BIN1
  N15: Arduino_Nano_Every.D8, Motor_Driver.BIN2
  N16: Arduino_Nano_Every.D9~, Motor_Driver.PWMA
  N17: Arduino_Nano_Every.D10~, Motor_Driver.PWMB
  N18: Arduino_Nano_Every.D11/MOSI, PS2_Receiver.pin2, R3.Pin_0, R3.Pin_1
  N19: Arduino_Nano_Every.D12~/MISO, PS2_Receiver.pin1
  N20: Arduino_Nano_Every.A0, PS2_Receiver.pin5, R1.Pin_0, R1.Pin_1
  N21: Arduino_Nano_Every.3V3, PS2_Receiver.pin4
  N22: Arduino_Nano_Every.D13~, PS2_Receiver.pin6, R2.Pin_0, R2.Pin_1

notes:
  Left
  v1

custom parts:
  Boladge HMC5883L Compass Module: Cheap digital compass module
  Terminal 2pin: 2-pin Terminal Block
  Arduino Nano Every: The Nano Every is Arduino’s 5V compatible board in the smallest available form factor: 45x18mm! The Arduino Nano is the preferred board for many projects requiring a small and easy to use microcontroller board. The small footprint and low price, make the Nano Every particularly suited for wearable inventions, low cost robotics, electronic musical instruments, and general use to control smaller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
  Adafruit TB6612 DC and Stepper Motor Driver: Spin two DC motors, step one bi-polar or uni-polar stepper, or fire off two solenoids with 1.2A per channel using the TB6612. These are perhaps better known as "the drivers in our assembled Adafruit Motorshield or Motor HAT." We really like these dual H-bridges, so if you want to control motors without a shield or HAT these are easy to include on any solderless breadboard or perma-proto.
